# Fritzing sketch Gardena-lochraster (saved by Fritzing 1.0.7)
perfboards: 2

parts:
  U1 = attiny85 [package=dip]  # not connected
  J1 = screw terminal, 12 pins
  C1 = Electrolytic Capacitor [capacitance=1µF voltage=35V package="100 mil [THT, electrolytic]"]  # not connected
  C2 = Electrolytic Capacitor [capacitance=100µF voltage=16V package="100 mil [THT, electrolytic]"]  # not connected
  VCC1 = Battery [internal_resistance=0.1Ω]
  VCC2 = Battery [internal_resistance=0.1Ω]
  M1 = DC Motor [voltage_(max)=6V voltage_(min)=3V]
  JP1 = Header 1 [package=1x01_offset]  # not connected
  JP2 = Header 1 [package=1x01_offset]  # not connected
  JP3 = Header 1 [package=1x01_offset]  # not connected
  JP4 = Header 1 [package=1x01_offset]  # not connected
  JP5 = Header 1 [package=1x01_offset]  # not connected
  JP6 = Header 1 [package=1x01_offset]  # not connected
  JP7 = Header 1 [package=1x01_offset]  # not connected
  JP8 = Header 1 [package=1x01_offset]  # not connected
  JP9 = Header 1 [package=1x01_offset]  # not connected
  JP10 = Header 1 [package=1x01_offset]  # not connected
  JP11 = Header 1 [package=1x01_offset]  # not connected
  R1 = Resistor [tolerance=±5% power=0.25W resistance=47 package=THT]  # not connected
  D1 = Rectifier Diode [part_number=1N4001 package="300 mil [THT]"]  # not connected
  R2 = Resistor [tolerance=±5% power=0.25W resistance=10k package=THT]  # not connected
  C3 = Ceramic Capacitor [capacitance=100nF voltage=35V package="100 mil [THT, multilayer]"]  # not connected
  C4 = Ceramic Capacitor [capacitance=100nF voltage=35V package="100 mil [THT, multilayer]"]  # not connected

nets:
  N1: J1.pin1, VCC1.-
  N2: J1.pin2, VCC1.+
  N3: J1.pin3, VCC2.-
  N4: J1.pin4, VCC2.+
  N5: J1.pin11, M1.pin_1
  N6: J1.pin12, M1.pin_2
