# Fritzing sketch Attiny85-ArduinoUno (saved by Fritzing 1.0.7)
breadboards: 1

parts:
  Bauteil1 = Arduino Ethernet Shield (Rev3)
  C1 = Electrolytic Capacitor [capacitance=1μF voltage=35V package="0405 [SMD, electrolytic]"]
  U1 = attiny85 [package=dip]

nets:
  N1: Bauteil1.ETH_CS, U1.Pin_1
  N2: Bauteil1.PWM_D11, U1.Pin_5
  N3: Bauteil1.SPI/D12, U1.Pin_6
  N4: Bauteil1.SPI/D13, U1.Pin_7
  N5: Bauteil1.RESET, C1.+
  N6: Bauteil1.5V, U1.Pin_8
  N7: Bauteil1.GND, C1.-, U1.Pin_4
